# Fritzing sketch magnetic encoder servo fritzing (saved by Fritzing 0.9.3b)
breadboards: 1

parts:
  U1 = MAG-ENC [chip_label="MAGNETIC ROTARY ENCODER" package="SIP (Single Inline) [THT]"]
  L298N1 = L298N DC motor driver
  Mod1 = Raspberry Pi Pico
  U2 = MAG-ENC [chip_label="MAGNETIC ROTARY ENCODER" package="SIP (Single Inline) [THT]"]
  M1 = DC Motor
  VCC1 = Battery block 9V

nets:
  VCC: U1.VCC, L298N1.5V, Mod1.pin_36, U2.VCC
  N1: U1.EI-INT1, Mod1.pin_6
  N2: U1.E1-INT2, Mod1.pin_7
  N3: U1.E2-INT1, Mod1.pin_9
  N4: U1.E2-INT2, Mod1.pin_10
  GND: U1.GND, L298N1.GND, Mod1.pin_8, Mod1.pin_18, Mod1.pin_33, Mod1.pin_38, U2.GND, VCC1.-
  N5: L298N1.OUT1, M1.pin_2
  N6: L298N1.OUT2, M1.pin_1
  N7: L298N1.12V, VCC1.+
  N8: L298N1.IN1, Mod1.pin_17
  N9: L298N1.IN2, Mod1.pin_16
  N10: Mod1.pin_20, U2.LED
  N11: Mod1.pin_21, U2.EI-INT1
  N12: Mod1.pin_22, U2.E1-INT2
  N13: Mod1.pin_24, U2.E2-INT1
  N14: Mod1.pin_25, U2.E2-INT2

notes:
  SERVO ENCODER
  CONTROL ENCODER

custom parts:
  MAG-ENC: AHMSVILLE LABS Standalone Magnetic Rotary Encoder
  L298N DC motor driver: 2x DC motor driver with 78M05 positive voltage regulator (7..35 V) L298N: max 46 V, 2 A Set 5 V Enable jumper to enable 5 V regultor (needed for the L298N) and +5 V output at screw terminal or supply external +5 V at screw terminal Set ENA and/or ENB to +5 V to enable motor permanently or supply ENA and/or ENB with PWM signal IN1 and IN2 set rotation directory for motor A (OUT1/OUT2) IN2 and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
  Raspberry Pi Pico: Raspberry Pi Pico. Based around the RP2040 microcontroller the Pico is a low cost microcontroller device bringing Raspberry Pi quality, cost, and easy of use to the microcontroller space. Jan 2021, Split part in to two versions: SMD (this one) and tht. This one is single sided and uses the castellation pads to solder the module to the board (no holes, other than for the USB connector!). The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
